# Fritzing sketch bjt (saved by Fritzing 0.9.2b)
breadboards: 1

parts:
  Q1 = NPN-Transistor [package="SOT-23 [SMD]"]  # not connected
  R_pi = Resistor [tolerance=±5% resistance=220 package=THT]
  Ro = Resistor [tolerance=±5% resistance=220 package=THT]
  Fonte_de_corrente = mystery part, 4 pins

nets:
  N1: R_pi.Pin_0, Fonte_de_corrente.pin3
  5V: R_pi.Pin_1, Ro.Pin_0, Ro.Pin_1, Fonte_de_corrente.pin1, Fonte_de_corrente.pin2, Fonte_de_corrente.pin4

notes:
  B
  C
  E
