# Fritzing sketch diode (saved by Fritzing 0.9.2b)
breadboards: 1

parts:
  part = DC Power [voltage=1.1V]
  D1 = Rectifier Diode [part_number=1N4001 package="300 mil [THT]"]

nets:
  GND: part.V+
  N1: part.V-, D1.cathode
  5V: D1.anode
