# Fritzing sketch diode2 (saved by Fritzing 0.9.2b)
breadboards: 1

parts:
  part = DC Power [voltage=1.1V]
  part_2 = Rectifier Diode [part_number=1N4007 package="300 mil [THT]"]

nets:
  GND: part.V+
  N1: part.V-, part_2.cathode
  5V: part_2.anode
