# Fritzing sketch ex2 (saved by Fritzing 0.9.2b)
breadboards: 1

parts:
  U1 = LM386 [package=dip08]
  R1 = Resistor [tolerance=±5% resistance=220 package="0402 [SMD]"]
  R2 = Resistor [tolerance=±5% resistance=220 package="0402 [SMD]"]
  R3 = Resistor [tolerance=±5% resistance=220 package="0402 [SMD]"]

nets:
  N1: U1.-IN, R1.Pin_1, R2.Pin_0
  5V: U1.+IN, U1.OUT, R2.Pin_1, R3.Pin_0
  GND: R1.Pin_0, R3.Pin_1
