# Fritzing sketch c1 (saved by Fritzing 0.9.2b)
breadboards: 1

parts:
  D1 = Rectifier Diode [part_number=1N4001 package="300 mil [THT]"]
  R1 = Resistor [tolerance=±5% resistance=220 package=THT]

nets:
  5V: D1.cathode, D1.anode, R1.Pin_0
  GND: R1.Pin_1
