# Fritzing sketch c2 (saved by Fritzing 0.9.2b)
breadboards: 1

parts:
  D1 = Rectifier Diode [part_number=1N4007 package="300 mil [THT]"]
  R1 = Resistor [tolerance=±5% resistance=1k package=THT]

nets:
  5V: D1.cathode, R1.Pin_0
  10V: D1.anode
  GND: R1.Pin_1

notes:
  Vs
  V
