# Fritzing sketch c3 (saved by Fritzing 0.9.2b)
breadboards: 1

parts:
  D1 = Rectifier Diode [part_number=1N4007 package="300 mil [THT]"]
  R1 = Resistor [tolerance=±5% resistance=1k package=THT]
  D2 = Rectifier Diode [part_number=1N4007 package="300 mil [THT]"]

nets:
  GND: D1.cathode, D2.anode
  5V: D1.anode, R1.Pin_1, D2.cathode
  10V: R1.Pin_0

notes:
  Vs
  V
