# Fritzing sketch c4 (saved by Fritzing 0.9.2b)
breadboards: 1

parts:
  R1 = Resistor [tolerance=±5% resistance=1k package=THT]
  DZ = Zener Diode [breakdown_voltage=3.6V package="300 mil [THT]"]

nets:
  10V: R1.Pin_0
  5V: R1.Pin_1, DZ.cathode
  GND: DZ.anode

notes:
  Vs
  V
