# Fritzing sketch ex1 (saved by Fritzing 0.9.2b)
breadboards: 1

parts:
  VD = DC Power [voltage=1.1V]
  C = Ceramic Capacitor [package="100 mil [THT, multilayer]"]

nets:
  5V: VD.V+, VD.V-, C.1
  GND: C.0

notes:
  V
  Vo
