# Fritzing sketch ex2 (saved by Fritzing 0.9.2b)
breadboards: 1

parts:
  R = Resistor [tolerance=±5% resistance=220 package=THT]
  C = Ceramic Capacitor [capacitance=100nF package="100 mil [THT, multilayer]"]
  D1 = Rectifier Diode [part_number=1N4001 package="300 mil [THT]"]
  R1 = Resistor [tolerance=±5% resistance=220 package=THT]
  C1 = Ceramic Capacitor [capacitance=100nF package="100 mil [THT, multilayer]"]

nets:
  5V: R.Pin_0, C.1, D1.cathode, D1.anode, R1.Pin_0, C1.1
  GND: R.Pin_1, C.0, R1.Pin_1, C1.0

notes:
  V
  Vo
  (a)
  (b)
