# Fritzing sketch ex4-1 (saved by Fritzing 0.9.2b)
breadboards: 1

parts:
  D1 = Zener Diode [part_number=1N4739A breakdown_voltage=3.6V package="300 mil [THT]"]
  R1 = Resistor [tolerance=±5% resistance=470 package=THT]

nets:
  5V: D1.cathode, R1.Pin_0
  GND: D1.anode
  10V: R1.Pin_1

notes:
  e0
