# Fritzing sketch ex4-2 (saved by Fritzing 0.9.2b)
breadboards: 1

parts:
  R2 = Resistor [tolerance=±5% resistance=470 package=THT]
  RL = Resistor [tolerance=±5% resistance=4.7k package=THT]

nets:
  5V: R2.Pin_0, RL.Pin_1
  10V: R2.Pin_1
  GND: RL.Pin_0

notes:
  e0
