# Fritzing sketch ac_eq (saved by Fritzing 0.9.2b)
breadboards: 1

parts:
  Rs = Resistor [tolerance=±5% resistance=220 package=THT]
  Rb1 = Resistor [tolerance=±5% resistance=220 package=THT]
  Rb2 = Resistor [tolerance=±5% resistance=220 package=THT]
  Rl = Resistor [tolerance=±5% resistance=220 package=THT]
  Rc = Resistor [tolerance=±5% resistance=220 package=THT]
  R_pi = Resistor [tolerance=±5% resistance=220 package=THT]
  Fonte_de_corrente1 = mystery part, 4 pins
  Ro = Resistor [tolerance=±5% resistance=220 package=THT]
  Vs = AC Power [voltage=5 frequency=60]

nets:
  N1: Rs.Pin_0, Vs.V+
  N2: Rs.Pin_1, Rb1.Pin_0, Rb2.Pin_1, R_pi.Pin_0
  GND: Rb1.Pin_1, Rb2.Pin_0, Rl.Pin_0, Rc.Pin_0, Fonte_de_corrente1.pin2, Fonte_de_corrente1.pin4, Ro.Pin_0, Vs.V-
  5V: Rl.Pin_1, Rc.Pin_1, Fonte_de_corrente1.pin1, Ro.Pin_1
  N3: R_pi.Pin_1, Fonte_de_corrente1.pin3

notes:
  Vo
