# Fritzing sketch circuit (saved by Fritzing 0.9.2b)
breadboards: 1

parts:
  Rs = Resistor [tolerance=±5% resistance=220 package=THT]
  C1 = Tantalum Capacitor [capacitance=1μF package="100 mil [THT, tantalum]"]
  Rb1 = Resistor [tolerance=±5% resistance=220 package=THT]
  Rb2 = Resistor [tolerance=±5% resistance=220 package=THT]
  Q1 = NPN-Transistor [package="TO92 [THT]"]
  Re = Resistor [tolerance=±5% resistance=220 package=THT]
  C2 = Tantalum Capacitor [capacitance=1μF package="100 mil [THT, tantalum]"]
  C3 = Tantalum Capacitor [capacitance=1μF package="100 mil [THT, tantalum]"]
  Rl = Resistor [tolerance=±5% resistance=220 package=THT]
  Vs = DC Power [voltage=5]
  Rc = Resistor [tolerance=±5% resistance=220 package=THT]

nets:
  N1: Rs.Pin_0, Vs.V+
  N2: Rs.Pin_1, C1.+
  N3: C1.-, Rb1.Pin_0, Rb2.Pin_1, Q1.B
  5V: Rb1.Pin_1, C3.-, Rl.Pin_1, Rc.Pin_1
  GND: Rb2.Pin_0, Re.Pin_0, C2.-, Rl.Pin_0, Vs.V-
  N4: Q1.E, Re.Pin_1, C2.+
  N5: Q1.C, C3.+, Rc.Pin_0

notes:
  Vo
