# Fritzing sketch ex4i (saved by Fritzing 0.9.2b)
breadboards: 1

parts:
  Rc_||_Rl = Resistor [tolerance=±5% resistance=220 package=THT]
  R_pi = Resistor [tolerance=±5% resistance=220 package=THT]
  Fonte_de_corrente = mystery part, 4 pins
  Ro = Resistor [tolerance=±5% resistance=220 package=THT]

nets:
  GND: Rc_||_Rl.Pin_0, Fonte_de_corrente.pin2, Fonte_de_corrente.pin4, Ro.Pin_0
  5V: Rc_||_Rl.Pin_1, R_pi.Pin_0, Fonte_de_corrente.pin1, Ro.Pin_1
  N1: R_pi.Pin_1, Fonte_de_corrente.pin3

notes:
  Vo
  Vth
