# Fritzing sketch ex4o (saved by Fritzing 0.9.2b)
breadboards: 1

parts:
  Rs = Resistor [tolerance=±5% resistance=220 package=THT]
  Rb = Resistor [tolerance=±5% resistance=220 package=THT]
  Rc_||_Rl = Resistor [tolerance=±5% resistance=220 package=THT]
  R_pi = Resistor [tolerance=±5% resistance=220 package=THT]
  Fonte_de_corrente = mystery part, 4 pins [chip_label=?]
  Ro = Resistor [tolerance=±5% resistance=220 package=THT]
  Vs = AC Power [voltage=5 frequency=60]

nets:
  N1: Rs.Pin_0, Vs.V+
  N2: Rs.Pin_1, Rb.Pin_0, R_pi.Pin_0
  GND: Rb.Pin_1, Rc_||_Rl.Pin_0, Fonte_de_corrente.pin2, Fonte_de_corrente.pin4, Ro.Pin_0, Vs.V-
  5V: Rc_||_Rl.Pin_1, Fonte_de_corrente.pin1, Ro.Pin_1
  N3: R_pi.Pin_1, Fonte_de_corrente.pin3

notes:
  Vth
